# Fritzing sketch hue_numpad (saved by Fritzing 0.9.3b)
circuit board: 8.46667cm x 5.64444cm
breadboards: 1

parts:
  U1 = ESP8266 WiFi Module [part_number=ESP8266]
  Part1 = Breadboard Power Supply Board SMD
  R1 = Resistor [tolerance=±5% resistance=220 package=THT]
  R2 = Resistor [tolerance=±5% resistance=220 package=THT]
  R3 = Resistor [tolerance=±5% resistance=220 package=THT]
  R4 = Resistor [tolerance=±5% resistance=220 package=THT]
  Matrix_keypad1 = KEYPAD 4x4

nets:
  VCC: U1.VCC, Part1.VCC, R1.Pin_1, R2.Pin_1, R3.Pin_1, R4.Pin_1
  N1: U1.GPIO_0, Matrix_keypad1.row2
  N2: U1.GPIO_2, Matrix_keypad1.row3
  GND: U1.GND, Part1.GND
  N3: U1.GPIO_15, Matrix_keypad1.row4
  N4: U1.GPIO_4, Matrix_keypad1.row1
  N5: U1.GPIO_16, R4.Pin_0, Matrix_keypad1.col4
  N6: U1.GPIO_14, R3.Pin_0, Matrix_keypad1.col3
  N7: U1.GPIO_12, R2.Pin_0, Matrix_keypad1.col2
  N8: U1.GPIO_13, R1.Pin_0, Matrix_keypad1.col1

custom parts:
  KEYPAD 4x4: Matrix keypad 16 buttons, 4 rows x 4 columns
